// Digital circuit Inv.dig as structural Verilog
module Inv (
  input  n_1,
  input  n_2,
  input  n_3,
  output val2,
  output val1,
  output val3
);

  nand nand_1 (val1, n_1, n_1);
  nand nand_2 (val2, n_2, n_2);
  nand nand_3 (val3, n_3, n_3);

  // Notes on the sheet:
  //   INV CI
endmodule
