// Digital circuit main.dig as structural Verilog
module main (
  input  n_A,
  input  n_B,
  input  clock,
  input  enable,
  input  op_1,
  input  op_2,
  input  op_3,
  input  addr_1,
  input  addr_2,
  input  addr_3,
  input  data_unused
);

  wire _1_bit_register_1_q, _1_bit_register_2_q, _1_bit_register_3_q, _1_bit_register_4_q,
       _1_bit_register_5_q, _1_bit_register_6_q, _1_bit_register_7_q, _1_bit_register_8_q,
       _4_bit_adder_1_c_out, _4_bit_adder_1_res_1, _4_bit_adder_1_res_2, _4_bit_adder_1_res_3,
       _4_bit_adder_1_res_4, _4_bit_inverter_1_val1, _4_bit_inverter_1_val2, _4_bit_inverter_1_val3,
       _4_bit_inverter_1_val4, _7_segment_1_bot_1, _7_segment_1_bot_2, _7_segment_1_bot_3,
       _7_segment_1_bot_4, _7_segment_1_top_1, _7_segment_1_top_2, _7_segment_1_top_3, _7_segment_1_top_4,
       _8x1_mux_1_val, _8x1_mux_2_val, _8x1_mux_3_val, _8x1_mux_4_val, A_val_1, A_val_2, A_val_3, A_val_4,
       B_val_1, B_val_2, B_val_3, B_val_4, C_val_1, C_val_2, C_val_3, C_val_4;

  _1_bit_Register _1_bit_register_1 (.data(n_A), .enable(enable), .clock(clock), .Q(_1_bit_register_1_q));
  _1_bit_Register _1_bit_register_2 (.data(n_B), .enable(enable), .clock(clock), .Q(_1_bit_register_2_q));
  _1_bit_Register _1_bit_register_3 (
    .data(_1_bit_register_1_q), .enable(enable), .clock(clock), .Q(_1_bit_register_3_q));
  _1_bit_Register _1_bit_register_4 (
    .data(_1_bit_register_2_q), .enable(enable), .clock(clock), .Q(_1_bit_register_4_q));
  _1_bit_Register _1_bit_register_5 (
    .data(_1_bit_register_3_q), .enable(enable), .clock(clock), .Q(_1_bit_register_5_q));
  _1_bit_Register _1_bit_register_6 (
    .data(_1_bit_register_4_q), .enable(enable), .clock(clock), .Q(_1_bit_register_6_q));
  _1_bit_Register _1_bit_register_7 (
    .data(_1_bit_register_5_q), .enable(enable), .clock(clock), .Q(_1_bit_register_7_q));
  _1_bit_Register _1_bit_register_8 (
    .data(_1_bit_register_6_q), .enable(enable), .clock(clock), .Q(_1_bit_register_8_q));
  _4_bit_Register A (
    .enable(enable), .clock(clock), .n_1(_1_bit_register_1_q), .n_2(_1_bit_register_3_q),
    .n_3(_1_bit_register_5_q), .n_4(_1_bit_register_7_q), .val_1(A_val_1), .val_2(A_val_2), .val_3(A_val_3),
    .val_4(A_val_4));
  _4_bit_Register B (
    .enable(enable), .clock(clock), .n_1(_1_bit_register_2_q), .n_2(_1_bit_register_4_q),
    .n_3(_1_bit_register_6_q), .n_4(_1_bit_register_8_q), .val_1(B_val_1), .val_2(B_val_2), .val_3(B_val_3),
    .val_4(B_val_4));
  LED led_1 (.in(A_val_1));
  LED led_2 (.in(A_val_2));
  LED led_3 (.in(A_val_3));
  LED led_4 (.in(B_val_1));
  LED led_5 (.in(B_val_2));
  LED led_6 (.in(A_val_4));
  LED led_7 (.in(B_val_3));
  LED led_8 (.in(B_val_4));
  _4_bit_Inverter _4_bit_inverter_1 (
    .val2(_4_bit_inverter_1_val2), .val1(_4_bit_inverter_1_val1), .val3(_4_bit_inverter_1_val3),
    .val4(_4_bit_inverter_1_val4));
  _4_bit_Adder _4_bit_adder_1 (
    .n1_1(A_val_1), .n1_2(A_val_2), .n1_3(A_val_3), .n1_4(A_val_4), .n2_1(B_val_1), .n2_2(B_val_2),
    .res_1(_4_bit_adder_1_res_1), .res_2(_4_bit_adder_1_res_2), .res_3(_4_bit_adder_1_res_3),
    .res_4(_4_bit_adder_1_res_4), .n2_3(B_val_3), .n2_4(B_val_4), .C_out(_4_bit_adder_1_c_out));
  LED led_9 (.in(_4_bit_adder_1_c_out));
  _8x1_Mux _8x1_mux_1 (
    .select_1(op_1), .select_2(op_2), .select_3(op_3), .data_1(data_unused), .data_3(_4_bit_inverter_1_val1),
    .data_5(data_unused), .data_7(data_unused), .data_2(data_unused), .data_4(_4_bit_adder_1_res_1),
    .data_6(data_unused), .data_8(data_unused), .val(_8x1_mux_1_val));
  _8x1_Mux _8x1_mux_2 (
    .select_1(op_1), .select_2(op_2), .select_3(op_3), .data_1(data_unused), .data_3(_4_bit_inverter_1_val2),
    .data_5(data_unused), .data_7(data_unused), .data_2(data_unused), .data_4(_4_bit_adder_1_res_2),
    .data_6(data_unused), .data_8(data_unused), .val(_8x1_mux_2_val));
  _8x1_Mux _8x1_mux_3 (
    .select_1(op_1), .select_2(op_2), .select_3(op_3), .data_1(data_unused), .data_3(_4_bit_inverter_1_val3),
    .data_5(data_unused), .data_7(data_unused), .data_2(data_unused), .data_4(_4_bit_adder_1_res_3),
    .data_6(data_unused), .data_8(data_unused), .val(_8x1_mux_3_val));
  _8x1_Mux _8x1_mux_4 (
    .select_1(op_1), .select_2(op_2), .select_3(op_3), .data_1(data_unused), .data_3(_4_bit_inverter_1_val4),
    .data_5(data_unused), .data_7(data_unused), .data_2(data_unused), .data_4(_4_bit_adder_1_res_4),
    .data_6(data_unused), .data_8(data_unused), .val(_8x1_mux_4_val));
  LED led_10 (.in(_8x1_mux_1_val));
  LED led_11 (.in(_8x1_mux_2_val));
  LED led_12 (.in(_8x1_mux_3_val));
  LED led_13 (.in(_8x1_mux_4_val));
  _4_bit_Register C (
    .enable(enable), .clock(clock), .n_1(_8x1_mux_1_val), .n_2(_8x1_mux_2_val), .n_3(_8x1_mux_3_val),
    .n_4(_8x1_mux_4_val), .val_1(C_val_1), .val_2(C_val_2), .val_3(C_val_3), .val_4(C_val_4));
  LED led_14 (.in(C_val_1));
  LED led_15 (.in(C_val_2));
  LED led_16 (.in(C_val_3));
  LED led_17 (.in(C_val_4));
  _7_Segment _7_segment_1 (
    .top_1(_7_segment_1_top_1), .top_2(_7_segment_1_top_2), .top_3(_7_segment_1_top_3),
    .top_4(_7_segment_1_top_4), .bot_1(_7_segment_1_bot_1), .bot_2(_7_segment_1_bot_2),
    .bot_3(_7_segment_1_bot_3), .bot_4(_7_segment_1_bot_4));
  Seven_Seg seven_seg_1 (
    .a(_7_segment_1_top_1), .b(_7_segment_1_top_2), .c(_7_segment_1_top_3), .d(_7_segment_1_top_4),
    .e(_7_segment_1_bot_1), .f(_7_segment_1_bot_2), .g(_7_segment_1_bot_3), .dp(_7_segment_1_bot_4));

  // Notes on the sheet:
  //   enable: default 1
  //   op_2: default 1
  //   op_3: default 1
endmodule
